// Digital circuit RippleCarryAdder.dig as structural Verilog
module RippleCarryAdder (
  input  A0,
  input  A1,
  input  A2,
  input  A3,
  input  B0,
  input  B1,
  input  B2,
  input  B3,
  input  C_in,
  output S0,
  output S1,
  output S2,
  output S3,
  output C_Out
);

  Add Adder3 ();  // open: a, b, c_i, s, c_o
  Add Adder2 ();  // open: a, b, c_i, s, c_o
  Add Adder1 ();  // open: a, b, c_i, s, c_o
  Add Adder0 ();  // open: a, b, c_i, s, c_o
endmodule

/* Test case:
A3	A2	A1	A0	B3	B2	B1	B0	C_Out	S3	S2	S1	S0
0	0	0	0	0	0	0	0	0	0	0	0	0
0	0	0	1	0	0	0	0	0	0	0	0	1
0	0	1	0	0	0	0	0	0	0	0	1	0
0	0	1	1	0	0	0	0	0	0	0	1	1
0	1	0	0	0	0	0	0	0	0	1	0	0
0	1	0	1	0	0	0	0	0	0	1	0	1
0	1	1	0	0	0	0	0	0	0	1	1	0
0	1	1	1	0	0	0	0	0	0	1	1	1
1	0	0	0	0	0	0	0	0	1	0	0	0
1	0	0	1	0	0	0	0	0	1	0	0	1
1	0	1	0	0	0	0	0	0	1	0	1	0
1	0	1	1	0	0	0	0	0	1	0	1	1
1	1	0	0	0	0	0	0	0	1	1	0	0
1	1	0	1	0	0	0	0	0	1	1	0	1
1	1	1	0	0	0	0	0	0	1	1	1	0
1	1	1	1	0	0	0	0	0	1	1	1	1
0	0	0	0	0	0	0	1	0	0	0	0	1
0	0	0	1	0	0	0	1	0	0	0	1	0
0	0	1	0	0	0	0	1	0	0	0	1	1
0	0	1	1	0	0	0	1	0	0	1	0	0
0	1	0	0	0	0	0	1	0	0	1	0	1
0	1	0	1	0	0	0	1	0	0	1	1	0
0	1	1	0	0	0	0	1	0	0	1	1	1
0	1	1	1	0	0	0	1	0	1	0	0	0
1	0	0	0	0	0	0	1	0	1	0	0	1
1	0	0	1	0	0	0	1	0	1	0	1	0
1	0	1	0	0	0	0	1	0	1	0	1	1
1	0	1	1	0	0	0	1	0	1	1	0	0
1	1	0	0	0	0	0	1	0	1	1	0	1
1	1	0	1	0	0	0	1	0	1	1	1	0
1	1	1	0	0	0	0	1	0	1	1	1	1
1	1	1	1	0	0	0	1	1	0	0	0	0
0	0	0	0	0	0	1	0	0	0	0	1	0
0	0	0	1	0	0	1	0	0	0	0	1	1
0	0	1	0	0	0	1	0	0	0	1	0	0
0	0	1	1	0	0	1	0	0	0	1	0	1
0	1	0	0	0	0	1	0	0	0	1	1	0
0	1	0	1	0	0	1	0	0	0	1	1	1
0	1	1	0	0	0	1	0	0	1	0	0	0
0	1	1	1	0	0	1	0	0	1	0	0	1
1	0	0	0	0	0	1	0	0	1	0	1	0
1	0	0	1	0	0	1	0	0	1	0	1	1
1	0	1	0	0	0	1	0	0	1	1	0	0
1	0	1	1	0	0	1	0	0	1	1	0	1
1	1	0	0	0	0	1	0	0	1	1	1	0
1	1	0	1	0	0	1	0	0	1	1	1	1
1	1	1	0	0	0	1	0	1	0	0	0	0
1	1	1	1	0	0	1	0	1	0	0	0	1
0	0	0	0	0	0	1	1	0	0	0	1	1
0	0	0	1	0	0	1	1	0	0	1	0	0
0	0	1	0	0	0	1	1	0	0	1	0	1
0	0	1	1	0	0	1	1	0	0	1	1	0
0	1	0	0	0	0	1	1	0	0	1	1	1
0	1	0	1	0	0	1	1	0	1	0	0	0
0	1	1	0	0	0	1	1	0	1	0	0	1
0	1	1	1	0	0	1	1	0	1	0	1	0
1	0	0	0	0	0	1	1	0	1	0	1	1
1	0	0	1	0	0	1	1	0	1	1	0	0
1	0	1	0	0	0	1	1	0	1	1	0	1
1	0	1	1	0	0	1	1	0	1	1	1	0
1	1	0	0	0	0	1	1	0	1	1	1	1
1	1	0	1	0	0	1	1	1	0	0	0	0
1	1	1	0	0	0	1	1	1	0	0	0	1
1	1	1	1	0	0	1	1	1	0	0	1	0
0	0	0	0	0	1	0	0	0	0	1	0	0
0	0	0	1	0	1	0	0	0	0	1	0	1
0	0	1	0	0	1	0	0	0	0	1	1	0
0	0	1	1	0	1	0	0	0	0	1	1	1
0	1	0	0	0	1	0	0	0	1	0	0	0
0	1	0	1	0	1	0	0	0	1	0	0	1
0	1	1	0	0	1	0	0	0	1	0	1	0
0	1	1	1	0	1	0	0	0	1	0	1	1
1	0	0	0	0	1	0	0	0	1	1	0	0
1	0	0	1	0	1	0	0	0	1	1	0	1
1	0	1	0	0	1	0	0	0	1	1	1	0
1	0	1	1	0	1	0	0	0	1	1	1	1
1	1	0	0	0	1	0	0	1	0	0	0	0
1	1	0	1	0	1	0	0	1	0	0	0	1
1	1	1	0	0	1	0	0	1	0	0	1	0
1	1	1	1	0	1	0	0	1	0	0	1	1
0	0	0	0	0	1	0	1	0	0	1	0	1
0	0	0	1	0	1	0	1	0	0	1	1	0
0	0	1	0	0	1	0	1	0	0	1	1	1
0	0	1	1	0	1	0	1	0	1	0	0	0
0	1	0	0	0	1	0	1	0	1	0	0	1
0	1	0	1	0	1	0	1	0	1	0	1	0
0	1	1	0	0	1	0	1	0	1	0	1	1
0	1	1	1	0	1	0	1	0	1	1	0	0
1	0	0	0	0	1	0	1	0	1	1	0	1
1	0	0	1	0	1	0	1	0	1	1	1	0
1	0	1	0	0	1	0	1	0	1	1	1	1
1	0	1	1	0	1	0	1	1	0	0	0	0
1	1	0	0	0	1	0	1	1	0	0	0	1
1	1	0	1	0	1	0	1	1	0	0	1	0
1	1	1	0	0	1	0	1	1	0	0	1	1
1	1	1	1	0	1	0	1	1	0	1	0	0
0	0	0	0	0	1	1	0	0	0	1	1	0
0	0	0	1	0	1	1	0	0	0	1	1	1
0	0	1	0	0	1	1	0	0	1	0	0	0
0	0	1	1	0	1	1	0	0	1	0	0	1
0	1	0	0	0	1	1	0	0	1	0	1	0
0	1	0	1	0	1	1	0	0	1	0	1	1
0	1	1	0	0	1	1	0	0	1	1	0	0
0	1	1	1	0	1	1	0	0	1	1	0	1
1	0	0	0	0	1	1	0	0	1	1	1	0
1	0	0	1	0	1	1	0	0	1	1	1	1
1	0	1	0	0	1	1	0	1	0	0	0	0
1	0	1	1	0	1	1	0	1	0	0	0	1
1	1	0	0	0	1	1	0	1	0	0	1	0
1	1	0	1	0	1	1	0	1	0	0	1	1
1	1	1	0	0	1	1	0	1	0	1	0	0
1	1	1	1	0	1	1	0	1	0	1	0	1
0	0	0	0	0	1	1	1	0	0	1	1	1
0	0	0	1	0	1	1	1	0	1	0	0	0
0	0	1	0	0	1	1	1	0	1	0	0	1
0	0	1	1	0	1	1	1	0	1	0	1	0
0	1	0	0	0	1	1	1	0	1	0	1	1
0	1	0	1	0	1	1	1	0	1	1	0	0
0	1	1	0	0	1	1	1	0	1	1	0	1
0	1	1	1	0	1	1	1	0	1	1	1	0
1	0	0	0	0	1	1	1	0	1	1	1	1
1	0	0	1	0	1	1	1	1	0	0	0	0
1	0	1	0	0	1	1	1	1	0	0	0	1
1	0	1	1	0	1	1	1	1	0	0	1	0
1	1	0	0	0	1	1	1	1	0	0	1	1
1	1	0	1	0	1	1	1	1	0	1	0	0
1	1	1	0	0	1	1	1	1	0	1	0	1
1	1	1	1	0	1	1	1	1	0	1	1	0
0	0	0	0	1	0	0	0	0	1	0	0	0
0	0	0	1	1	0	0	0	0	1	0	0	1
0	0	1	0	1	0	0	0	0	1	0	1	0
0	0	1	1	1	0	0	0	0	1	0	1	1
0	1	0	0	1	0	0	0	0	1	1	0	0
0	1	0	1	1	0	0	0	0	1	1	0	1
0	1	1	0	1	0	0	0	0	1	1	1	0
0	1	1	1	1	0	0	0	0	1	1	1	1
1	0	0	0	1	0	0	0	1	0	0	0	0
1	0	0	1	1	0	0	0	1	0	0	0	1
1	0	1	0	1	0	0	0	1	0	0	1	0
1	0	1	1	1	0	0	0	1	0	0	1	1
1	1	0	0	1	0	0	0	1	0	1	0	0
1	1	0	1	1	0	0	0	1	0	1	0	1
1	1	1	0	1	0	0	0	1	0	1	1	0
1	1	1	1	1	0	0	0	1	0	1	1	1
0	0	0	0	1	0	0	1	0	1	0	0	1
0	0	0	1	1	0	0	1	0	1	0	1	0
0	0	1	0	1	0	0	1	0	1	0	1	1
0	0	1	1	1	0	0	1	0	1	1	0	0
0	1	0	0	1	0	0	1	0	1	1	0	1
0	1	0	1	1	0	0	1	0	1	1	1	0
0	1	1	0	1	0	0	1	0	1	1	1	1
0	1	1	1	1	0	0	1	1	0	0	0	0
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*/
